# Fritzing sketch Sketch10-pro_mini-RTC-SD-3WM (saved by Fritzing 0.9.3b)
breadboards: 1

parts:
  VCC2 = 4 x AAA Battery Mount
  ZS-042_RTC3 = ZS-042 RTC Module
  J1 = screw terminal, 2 pins
  R8 = Resistor [tolerance=±5% resistance=4.7k package=THT]
  D6 = Rectifier Diode [part_number=1N4342 package="300 mil [THT]"]
  D7 = Rectifier Diode [part_number=1N4342 package="300 mil [THT]"]
  R9 = Resistor [tolerance=±5% resistance=4.7k package=THT]
  Part4 = MicroSD Card Module
  Arduino1 = Arduino Pro Mini (5V)

nets:
  GND: VCC2.-, ZS-042_RTC3.GND, Part4.GND
  VCC: VCC2.+, ZS-042_RTC3.VCC, Part4.VCC
  N1: ZS-042_RTC3.SDA, Arduino1.A4
  N2: ZS-042_RTC3.SCL, Arduino1.A5
  N3: J1.pin1, R8.Pin_1, D6.cathode
  N4: J1.pin2, D7.cathode, R9.Pin_1
  N5: R8.Pin_0, R9.Pin_0

notes:
  ** Micro SD **
  VCC to 3.3 or 5v
  GND to GND
  D13 to SCK
  D11 to MOSI
  D12 to MISO
  D10 to CS
  ** RTC **
  VCC to 3.3 or 5v
  GND to GND
  SDA to A4
  SCL to A5
  SQW to A2
